# Fritzing sketch Medicine Scheduler (saved by Fritzing 0.9.3b)
breadboards: 1

parts:
  LED1 = LED - 5mm [color="Yellow (592nm)" package="5 mm [THT]"]
  LED2 = LED - 5mm [color="Yellow (592nm)" package="5 mm [THT]"]
  LED3 = LED - 5mm [color="Yellow (592nm)" package="5 mm [THT]"]
  LED4 = LED - 5mm [color="Yellow (592nm)" package="5 mm [THT]"]
  LED5 = LED - 5mm [color="Yellow (592nm)" package="5 mm [THT]"]
  Raspberry_Pi_Zero1 = Raspberry Pi Zero
  R1 = Resistor [tolerance=±5% resistance=220 package="2010 [SMD]"]
  R2 = Resistor [tolerance=±5% resistance=220 package="2010 [SMD]"]
  R3 = Resistor [tolerance=±5% resistance=220 package="2010 [SMD]"]
  R4 = Resistor [tolerance=±5% resistance=220 package="2010 [SMD]"]
  R5 = Resistor [tolerance=±5% resistance=220 package="2010 [SMD]"]
  LED6 = LED - 5mm [color="Yellow (592nm)" package="5 mm [THT]"]
  LED7 = LED - 5mm [color="Yellow (592nm)" package="5 mm [THT]"]
  R6 = Resistor [tolerance=±5% resistance=220 package="2010 [SMD]"]
  R7 = Resistor [tolerance=±5% resistance=220 package="2010 [SMD]"]
  ZS-042_RTC1 = ZS-042 RTC Module
  U1 = LCD-16X2 [package=lcd-16x2]
  R8 = Rotary Potentiometer (Large) [maximum_resistance=100kΩ package=THT]

nets:
  N1: LED1.cathode, R1.Pin_1
  N2: LED1.anode, Raspberry_Pi_Zero1.GPIO5
  N3: LED2.cathode, R5.Pin_1
  N4: LED2.anode, Raspberry_Pi_Zero1.GPIO27
  N5: LED3.cathode, R4.Pin_1
  N6: LED3.anode, Raspberry_Pi_Zero1.GPIO20, Raspberry_Pi_Zero1.GPIO16
  N7: LED4.cathode, R3.Pin_1
  N8: LED4.anode, Raspberry_Pi_Zero1.GPIO26, Raspberry_Pi_Zero1.GND, Raspberry_Pi_Zero1.GPIO12, LED6.anode, U1.RS
  N9: LED5.cathode, R2.Pin_1
  N10: LED5.anode, Raspberry_Pi_Zero1.GPIO6
  N11: Raspberry_Pi_Zero1.GPIO2, ZS-042_RTC1.SDA
  N12: Raspberry_Pi_Zero1.GPIO3, Raspberry_Pi_Zero1.GPIO4, ZS-042_RTC1.SCL
  N13: Raspberry_Pi_Zero1.GPIO17, U1.DB5
  N14: Raspberry_Pi_Zero1.GPIO22, U1.DB7
  N15: Raspberry_Pi_Zero1.GPIO13, Raspberry_Pi_Zero1.GPIO19, LED7.anode
  N16: Raspberry_Pi_Zero1.GPIO24, U1.E
  N17: Raspberry_Pi_Zero1.GPIO23, U1.DB4
  N18: Raspberry_Pi_Zero1.GPIO18, U1.DB6
  5V: Raspberry_Pi_Zero1.5V, U1.VDD
  GND: R1.Pin_0, R2.Pin_0, R3.Pin_0, R4.Pin_0, R5.Pin_0, R6.Pin_0, R7.Pin_0, ZS-042_RTC1.GND, U1.VSS, U1.R_W, U1.K, R8.leg2
  N19: LED6.cathode, R6.Pin_1
  N20: LED7.cathode, R7.Pin_1
  N21: ZS-042_RTC1.VCC, U1.A, R8.leg1
  N22: U1.VO, R8.wiper
